# Fritzing sketch Schem w pull-up (saved by Fritzing 0.9.3b)
breadboards: 1

parts:
  Part1 = Arduino Uno (Rev3)
  LED_IND = LED - 5mm [color="Yellow (585nm)" package="5 mm [THT]"]
  R1 = Resistor [tolerance=±5% resistance=220 package=THT]
  S1 = Pushbutton [package=THT]
  R_INT = Resistor [tolerance=±5% resistance=10k package=THT]
  K1 = Relay [part_number=FRS1B-S package=THT]
  D1 = Rectifier Diode [part_number=1N4004 package="300 mil [THT]"]
  R2 = Resistor [tolerance=±5% resistance=1k package=THT]
  Q1 = NPN-Transistor [package="TO92 [THT]"]
  R_RFOG = Resistor [tolerance=±5% resistance=220 package=THT]
  LED_RFOG = LED - 5mm [color="Red (633nm)" package="5 mm [THT]"]

nets:
  GND: Part1.GND, LED_IND.cathode, S1.leg1, Q1.E, LED_RFOG.cathode
  N1: Part1.D4, S1.leg0, R_INT.Pin_1
  N2: Part1.D5_PWM, R1.Pin_0
  N3: Part1.D7, R2.Pin_0
  N4: Part1.5V, K1.COIL2, D1.cathode
  N5: LED_IND.anode, R1.Pin_1
  5V: R_INT.Pin_0
  N6: K1.A, R_RFOG.Pin_0
  N7: K1.COIL1, D1.anode, Q1.C
  12V: K1.C2
  N8: R2.Pin_1, Q1.B
  N9: R_RFOG.Pin_1, LED_RFOG.anode
