# Fritzing sketch Schem (saved by Fritzing 0.9.3b)
breadboards: 1

parts:
  Part1 = Arduino Uno (Rev3)
  R_IND = Resistor [tolerance=±5% resistance=150 package=THT]
  S1 = Pushbutton [package=THT]
  R_INTERNAL = Resistor [tolerance=±5% resistance=20k package=THT]
  K1 = Relay [part_number=FRS1B-S package=THT]
  D1 = Rectifier Diode [part_number=1N4004 package="300 mil [THT]"]
  R2 = Resistor [tolerance=±5% resistance=1k package=THT]
  Q1 = NPN-Transistor [package="TO92 [THT]"]
  R_RFOG = Resistor [tolerance=±5% resistance=220 package=THT]
  LED_RFOG = LED - 5mm [color="Red (633nm)" package="5 mm [THT]"]
  LED_IND = LED - 3mm [color="Yellow (585nm)" package="3 mm [THT]"]

nets:
  GND: Part1.GND, S1.leg1, Q1.E, LED_RFOG.cathode, LED_IND.cathode
  N1: Part1.D4, S1.leg0, R_INTERNAL.Pin_1
  N2: Part1.D5_PWM, R_IND.Pin_0
  N3: Part1.D7, R2.Pin_0
  N4: Part1.5V, K1.COIL2, D1.cathode
  12V: Part1.VIN, K1.C2
  N5: R_IND.Pin_1, LED_IND.anode
  5V: R_INTERNAL.Pin_0
  N6: K1.A, R_RFOG.Pin_0
  N7: K1.COIL1, D1.anode, Q1.C
  N8: R2.Pin_1, Q1.B
  N9: R_RFOG.Pin_1, LED_RFOG.anode
